// Logisim project cpu.circ as structural Verilog: 4 circuits, main circuit cpu
module cpu (
  input  clk,
  input  ram_end,
  input  [31:0] ram_data,
  output [31:0] ram_read_addr,
  output cpu_end
);

  wire data_path_1_p11, data_path_1_p12, data_path_1_p13, data_path_1_p14, data_path_1_p15, data_path_1_p16,
       immediate, rw;
  wire [1:0] data_selector;
  wire [3:0] alu_selector;
  wire [4:0] register_d, register_s, register_t;
  wire [5:0] func_code, op_code;
  wire [25:0] jump;
  wire [31:0] constant, pc_next, ram;

  Register #(.width(32)) PC (.D(pc_next), .en(ram_end), .Q(ram_read_addr), .clk(clk));  // open: clr
  branch_control branch_control_1 (
    .PC_in(ram_read_addr), .jump(1'b0), .flag(1'b0), .offset({16{1'b0}}), .PC_out(pc_next));
  D_Flip_Flop d_ff_1 (.clk(clk), .D(ram_end), .Q(cpu_end));  // open: Qn, preset, en, reset
  instruction_decoder instruction_decoder_1 (
    .instruction(ram_data), .op_code(op_code), .Rs(register_s), .Rt(register_t), .Rd(register_d),
    .func_code(func_code), .constant(constant), .jump(jump), .alu_selector(alu_selector),
    .immediate(immediate), .d_in_selector(data_selector), .data_path_rw(rw));  // open: halt
  // data_path data_path_1: pin names not known; wires that end beside it: register_t, register_d, register_s, rw, constant, ram, ram_end, alu_selector, data_selector, immediate, data_path_1_p11, data_path_1_p12, data_path_1_p13, data_path_1_p14, data_path_1_p15, data_path_1_p16

  // Other names for the same wires on the sheet: end = ram_end; instruction[31:0] = ram_data;
  //   pc_current[31:0] = ram_read_addr
endmodule

module cpu_test (
);

  wire clock_1_out, \end , fake_ram_1_end;
  wire [31:0] addr, fake_ram_1_data;

  fake_ram fake_ram_1 (
    .cycles(4'b0000), .clk(clock_1_out), .db0(32'h1), .db1(32'h2), .db2(32'h3), .db3(32'h4), .ad(addr),
    .data(fake_ram_1_data), .\end (fake_ram_1_end), .cpu_end(\end ));  // open: real_addr
  // Probe on fake_ram_1_data
  Clock clock_1 (.out(clock_1_out));
  cpu cpu_1 (
    .ram_end(fake_ram_1_end), .ram_data(fake_ram_1_data), .ram_read_addr(addr), .clk(clock_1_out),
    .cpu_end(\end ));
  // Probe on addr
endmodule

module fake_ram (
  input  [3:0] cycles,
  input  clk,
  input  [31:0] db0,
  input  cpu_end,
  input  [31:0] db1,
  input  [31:0] db2,
  input  [31:0] db3,
  input  [31:0] ad,
  output [31:0] data,
  output \end ,
  output [15:0] real_addr
);

  wire [1:0] db_flag;
  wire [31:0] blocks;
  wire [31:2] divider_2_out;
  wire [31:16] arddr;

  Divider #(.width(32)) divider_1 (.a(ad), .b(32'h10), .out({arddr, real_addr}), .rem(blocks));  // open: upper
  Multiplexer #(.select(2), .width(32), .enable("false")) multiplexer_1 (
    .in0(db0), .in1(db1), .in2(db2), .in3(db3), .out(data), .sel(db_flag));
  Divider #(.width(32)) divider_2 (.a(blocks), .b(32'h4), .out({divider_2_out, db_flag}));  // open: upper, rem
  waita waita_1 (.cycles(cycles), .clk(clk), .cpu_end(cpu_end), .\end (\end ));

  // Other names for the same wires on the sheet: arddr[15:0] = real_addr; real_arddr[15:0] = real_addr
endmodule

module waita (
  input  clk,
  input  [3:0] cycles,
  input  cpu_end,
  output \end 
);

  wire not_1_out;
  wire [3:0] counter_1_q;

  Counter #(.width(4), .max('hf)) counter_1 (
    .count(not_1_out), .Q(counter_1_q), .clk(clk), .clr(cpu_end));  // open: load, D, carry
  not not_1 (not_1_out, \end );
  Comparator #(.width(4)) comparator_1 (.a(counter_1_q), .b(cycles), .eq(\end ));  // open: gt, lt
endmodule
